# Fritzing sketch CIRCUITO PARA MEDIR RITMO CARDIACO (saved by Fritzing 1.0.4)
breadboards: 1

parts:
  SEN1 = Pulse Sensor [package=SIP-3]
  M2 = DOIT Esp32 DevKit v1 (30 pins long, 11 pins width) [part_number=ESP32S-PIN30]

nets:
  N1: SEN1.Signal, M2.D34

custom parts:
  Pulse Sensor: Pulse Sensor Optical Heart Beat Sensor
  DOIT Esp32 DevKit v1 (30 pins long, 11 pins width): The DOIT Esp32 DevKit v1 is one of the development board created by DOIT to evaluate the ESP-WROOM-32 module. It is based on the ESP32 microcontroller that boasts Wifi, Bluetooth, Ethernet and Low Power support all in a single chip. (vanepp) made breadboard work, adjusted pin numbering and labels and reduced size of schematic and cleaned up pcb. This chip is 30pins long (2 x15) and 11 pins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
